# Fritzing sketch schematic (saved by Fritzing 0.9.3b)

parts:
  Part1 = Arduino Nano (Rev3.0)
  e-radionica_com1 = LM393 LDR breakout [part_number=100027]
  DHT11_1 = DHT11 module
  LED1 = smd LED [color="Yellow (592nm)" package="0603 [SMD]"]
  R1 = Resistor [tolerance=±5% resistance=220 package="0603 [SMD]"]
  U1 = L9110 H-bridge module [part_number="L9110 H-bridge"]  # not connected
  Part2 = LCD1602-I2C  # not connected

nets:
  GND: Part1.GND, e-radionica_com1.GND, DHT11_1.GND, LED1.cathode
  N1: Part1.D7, R1.Pin_0
  5V: Part1.5V, e-radionica_com1.VCC
  N2: Part1.A3, DHT11_1.DATA
  N3: Part1.A2, e-radionica_com1.AO
  3V3: Part1.3V3, DHT11_1.VCC
  N4: LED1.anode, R1.Pin_1

custom parts:
  DHT11 module: https://cdn-learn.adafruit.com/downloads/pdf/dht.pdf DHT11 black pcb module reference by:https://github.com/adafruit/Fritzing-Library/blob/master/parts/DHT11%20Humitidy%20and%20Temperature%20Sensor.fzpz
  LCD1602-I2C: A standard character display, usually with 2x16 characters. Comes in many colors with LCM1602 IIC attached.
